# Fritzing sketch trap (saved by Fritzing 0.9.3b)
circuit board: 6cm x 5.5cm
breadboards: 1

parts:
  arduino_nano = Arduino Nano (Rev3.0)
  T0 = npn-Powertransistor [package="TO220 [THT]"]
  R4 = Resistor [tolerance=±5% resistance=2.2k package=THT]
  R3 = Resistor [tolerance=±5% resistance=470 package=THT]
  R1 = Resistor [tolerance=±5% resistance=470 package=THT]
  R0 = Resistor [tolerance=±5% resistance=470 package=THT]
  J3 = female pin header, 3 pins [form="♀ (female)"]
  J2 = female pin header, 3 pins [form="♀ (female)"]
  J1 = female pin header, 3 pins [form="♀ (female)"]
  J0 = female pin header, 3 pins [form="♀ (female)"]
  R2 = Resistor [tolerance=±5% resistance=470 package=THT]
  Part1 = Real Time Clock Module - DS1307 RTC Breakout Board
  Part2 = MicroSD Card Module
  J4 = female pin header, 4 pins [form="♀ (female)"]
  J5 = female pin header, 6 pins [form="♀ (female)"]
  J6 = Power Jack [package=power_jack_slot]

nets:
  GND: arduino_nano.GND, T0.collector, Part1.GND, Part2.GND, J4.pin1, J5.pin6, J6.GND
  N1: arduino_nano.D3, R4.Pin_1
  N2: arduino_nano.D10, Part2.CS, J5.pin1
  N3: arduino_nano.D11/MOSI, Part2.MOSI, J5.pin3
  N4: arduino_nano.D12/MISO, Part2.MISO, J5.pin4
  N5: arduino_nano.VIN, J3.pin1, J2.pin1, J1.pin1, J0.pin1, J6.PWR
  5V: arduino_nano.5V, Part1.5V, Part2.VCC, J4.pin2, J5.pin5
  N6: arduino_nano.A5, Part1.SDA, J4.pin4
  N7: arduino_nano.A4, Part1.SCL, J4.pin3
  N8: arduino_nano.A3, R3.Pin_0, J3.pin3
  N9: arduino_nano.A2, J2.pin3, R2.Pin_0
  N10: arduino_nano.A1, R1.Pin_0, J1.pin3
  N11: arduino_nano.A0, R0.Pin_0, J0.pin3
  N12: arduino_nano.D13/SCK, Part2.SCK, J5.pin2
  N13: T0.base, R4.Pin_0
  N14: T0.emitter, R3.Pin_1, R1.Pin_1, R0.Pin_1, J3.pin2, J2.pin2, J1.pin2, J0.pin2, R2.Pin_1

// code stored in the sketch: smart_trap.ino
#include <RTClib.h>
#include <Wire.h>
#include <SPI.h>
#include <SdFat.h>
//#include <sdios.h>
//
#define OVER_SAMPLING 64
#define FS 8 // in Hz
#define RISE_TIME 100 // in microseconds
#define POWER_PIN 3

#define PHOTO_TRANSISTOR_N 4
#define PHOTO_TRANSISTOR_PINS {0,1,2,3}
#define LEARNING_RATE 0.01 // alpha
#define  Z_SCORE_THRESHOLD 4.753424 //R> qnorm(1 - 10^(-6),0,1)

#define error(msg) sd.errorHalt(F(msg))

// Log file base name.  Must be 2 characters.
#define FILE_BASE_NAME "st"

const float time_to_sleep_us = 1e6 / (FS * OVER_SAMPLING) - RISE_TIME;

RTC_DS1307 RTC;


// SD chip select pin.  Be sure to disable any other SPI devices such as Enet.
const uint8_t chipSelect = SS;
SdFat sd;
SdFile file;


int phototransistor_array[PHOTO_TRANSISTOR_N]= {0,1,2,3};
float rolling_mean[PHOTO_TRANSISTOR_N];
float rolling_sd[PHOTO_TRANSISTOR_N];
float former_accum[PHOTO_TRANSISTOR_N];

void writeHeader(){
    String header = "#";
  
    DateTime now = RTC.now(); 
  
    char datetime[17];
    sprintf (datetime, "%04d%02d%02d %02d:%02d:%02d",now.year(),now.month(),now.day(), now.hour(), now.minute(), now.second());
    header += datetime;
    
    file.print(header);
    Serial.println(header);
  //chip UID, date time,... gps?
}

// Log a data record.
String generateLogString(DateTime t, float x[]){
  String out = "";
  out += t.second();
  out += ',';
  
  for(int j =0; j < PHOTO_TRANSISTOR_N ; j++){
    out += x[j];
    out += ',';    
   }
   return out;
  }

void logDataSD(DateTime t, float x[]){
  file.println(generateLogString(t, x));
  // Force data to SD and update the directory entry to avoid data loss.
  if (!file.sync() || file.getWriteError()) {
    error("write error");
  }
}


void logDataSerial(DateTime t, float x[]){
  Serial.println(generateLogString(t, x));
}

void setup(void) {
    Serial.begin(57600);
    RTC.begin();
    Wire.begin();
    
    if (! RTC.isrunning()) {
      Serial.println("RTC is NOT running!");
      // This will reflect the time that your sketch was compiled
      RTC.adjust(DateTime(__DATE__, __TIME__));
    }
    pinMode(POWER_PIN, OUTPUT);

  const uint8_t BASE_NAME_SIZE = sizeof(FILE_BASE_NAME) - 1;
  char fileName[13] = FILE_BASE_NAME "0000.csv";


  // Initialize at the highest speed supported by the board that is
  // not over 50 MHz. Try a lower speed if SPI errors occur.
  if (!sd.begin(chipSelect, SD_SCK_MHZ(50))) {
    sd.initErrorHalt();
  }

  // Find an unused file name.
  if (BASE_NAME_SIZE > 2) {
    error("FILE_BASE_NAME too long");
  }
 
  
  while (sd.exists(fileName)) {
    if (fileName[BASE_NAME_SIZE + 3] != '9') {
      fileName[BASE_NAME_SIZE + 3]++;
    } else if (fileName[BASE_NAME_SIZE + 2] != '9') {
      fileName[BASE_NAME_SIZE + 3] = '0';
      fileName[BASE_NAME_SIZE + 2]++;
    } else if (fileName[BASE_NAME_SIZE + 1] != '9') {
      fileName[BASE_NAME_SIZE + 2] = '0';
      fileName[BASE_NAME_SIZE + 1]++;
    } else if (fileName[BASE_NAME_SIZE] != '9') {
      fileName[BASE_NAME_SIZE + 1] = '0';
      fileName[BASE_NAME_SIZE]++;
    } else {
      error("Can't create file name");
    }
  }
  if (!file.open(fileName, O_WRONLY | O_CREAT | O_EXCL)) {
    error("file.open");
  }
  writeHeader();
}

void loop(void) {
    float accum[PHOTO_TRANSISTOR_N];
    for(int j =0; j < PHOTO_TRANSISTOR_N ; j++){
      accum[j] = 0;
    }
    for(int i =0; i < OVER_SAMPLING; i++){
        digitalWrite(POWER_PIN, HIGH);
        delayMicroseconds(RISE_TIME);
        for(int j =0; j < PHOTO_TRANSISTOR_N ; j++){
          //Serial.println(phototransistor_array[j]);
          accum[j] +=  analogRead(phototransistor_array[j]);
        }
        digitalWrite(POWER_PIN, LOW);
        if(time_to_sleep_us > 16383)
            delay(time_to_sleep_us / 1e3);
        else
            delayMicroseconds(time_to_sleep_us);
    }
    for(int j =0; j < PHOTO_TRANSISTOR_N ; j++){
      accum[j] /= OVER_SAMPLING;
     }
 
    DateTime now = RTC.now(); 
    
/*
    float delt_accum = accum -former_accum;
    rolling_mean = rolling_mean * (1.0 -LEARNING_RATE) + LEARNING_RATE *delt_accum;
    float abs_diff = abs(rolling_mean -delt_accum );
    rolling_sd = rolling_sd * (1.0 - LEARNING_RATE) + LEARNING_RATE * abs_diff;
    former_accum=accum;
    float z_score = abs_diff / rolling_sd;
    bool crossing = false;
    if(z_score > Z_SCORE_THRESHOLD){
      crossing = true;
      }*/
    logDataSD(now, accum);
    logDataSerial(now, accum);
    

    /*
    Serial.print(now.year(), DEC);
    Serial.print('-');
    Serial.print(now.month(), DEC);
    Serial.print('-');
    Serial.print(now.day(), DEC);
    Serial.print(' ');
    Serial.print(now.hour(), DEC);
    Serial.print(':');
    Serial.print(now.minute(), DEC);
    Serial.print(':');
    Serial.print(now.second(), DEC);
    Serial.print('|');
    Serial.print(accum);
    Serial.print('|');
    Serial.print(delt_accum);
    Serial.print('|');
    Serial.print(rolling_mean);
    Serial.print('|');
    Serial.print(rolling_sd);
    Serial.print('|');
    Serial.println(crossing);
    
*/
}
